# Fritzing sketch RGBPi_Fritzing (saved by Fritzing 0.9.2b)
breadboards: 1

parts:
  Raspberry_Pi1 = Raspberry Pi 2
  Q1 = TIP120 Hi-Current Darlington Transistor
  Q2 = TIP120 Hi-Current Darlington Transistor
  Q3 = TIP120 Hi-Current Darlington Transistor
  Power_plug1 = Power plug
  Bauteil1 = Arduino Mini Proto Shield

nets:
  N1: Raspberry_Pi1.GPIO12, Q3.BASE
  GND: Raspberry_Pi1.GND, Q2.BASE, Power_plug1.GND
  N2: Raspberry_Pi1.GPIO7, Q1.BASE
  N3: Q1.COLLECTOR, Bauteil1.N$9
  N4: Q2.COLLECTOR, Bauteil1.N$1
  N5: Q3.COLLECTOR, Bauteil1.N$33
  N6: Power_plug1.VCC, Bauteil1.N$10
